# Fritzing sketch avisa-te (saved by Fritzing 0.9.3b)
circuit board: 7cm x 5cm
breadboards: 1

parts:
  LED1 = RGB LED (com. cathode, rgb) [package="5 mm [THT]"]
  WeMos_D1_Mini1 = WeMos D1 Mini
  zumbador = KY-012 Active Buzzer Module [package="Breakout board"]
  mlx90614 = BME280
  R1 = Resistor [tolerance=±5% resistance=220 package=THT]
  R2 = Resistor [tolerance=±5% resistance=220 package=THT]
  vl6180x = Adafruit VL6180X Time of Flight Distance Sensor [part_number="Adafruit #3316"]
  R3 = Resistor [tolerance=±5% resistance=220 package=THT]

nets:
  N1: LED1.red_anode, R3.Pin_0
  GND: LED1.common_cathode, WeMos_D1_Mini1.G, zumbador.-, mlx90614.GND, vl6180x.GND
  N2: LED1.green_anode, R1.Pin_1
  N3: LED1.blue_anode, R2.Pin_1
  VIN: WeMos_D1_Mini1.3V3, zumbador.S, mlx90614.VIN, vl6180x.VIN
  N4: WeMos_D1_Mini1.D1, mlx90614.SCL, vl6180x.SCL
  N5: WeMos_D1_Mini1.D2, mlx90614.SDA, vl6180x.SDA
  N6: WeMos_D1_Mini1.D5, R3.Pin_1
  N7: WeMos_D1_Mini1.D6, R1.Pin_0
  N8: WeMos_D1_Mini1.D7, zumbador.NC
  N9: WeMos_D1_Mini1.D8, R2.Pin_0

custom parts:
  KY-012 Active Buzzer Module: Active Piezoelectric Buzzer Module KY-012, it produces single-tone sound when signal is high. (Special thanks to vanepp for fixing the PCB holes and other errors)
  BME280: Temperature Humidity Barometric presure Sensor
  Adafruit VL6180X Time of Flight Distance Sensor: The VL6180X is a Time of Flight distance sensor like no other you've used! The sensor contains a very tiny invisible laser source, and a matching sensor. The VL6180X can detect the "time of flight", or how long the light has taken to bounce back to the sensor. Since it uses a very narrow light source, it is good for determining distance of only the surface directly in front of it. Unlike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
